# Fritzing sketch Project_Fritzing (saved by Fritzing 0.9.3b)
circuit board: 4.28912cm x 2.76053cm
breadboards: 1

parts:
  Pulse_Sensor = Pulse Sensor [package=SIP]
  ADS1015 = Adafruit ADS1015 12Bit I2C ADC [part_number="Adafruit #1083"]
  J1 = double row male pin header, 10 pins [form="♂ (male)"]

nets:
  VCC: Pulse_Sensor.Vcc, ADS1015.VDD, J1.pin1
  GND: Pulse_Sensor.GND, ADS1015.GND, J1.pin6
  N1: Pulse_Sensor.Signal, ADS1015.AIN0
  N2: ADS1015.SDA, J1.pin3
  N3: ADS1015.SCL, J1.pin5

notes:
  Quyen Lu
  3.3V
  SDA
  SCL
  Ground

custom parts:
  Pulse Sensor: Pulse Sensor Optical Heart Rate Monitor for Arduino and other microcontrollers
  Adafruit ADS1015 12Bit I2C ADC: For microcontrollers without an analog-to-digital converter or when you want a higher-precision ADC, the ADS1015 provides 12-bit precision at 3300 samples/second over I2C. The chip can be configured as 4 single-ended input channels, or two differential channels. As a nice bonus, it even includes a programmable gain amplifier, up to x16, to help boost up smaller single/differential signals to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
